# Fritzing sketch prueba2 (saved by Fritzing 0.9.5d)
breadboards: 1

parts:
  Raspberry_Pi_1 = Raspberry Pi 3 [part_number=RPI-3-V1.2]
  S1 = Pushbutton [package="[THT]"]
  S2 = Pushbutton [package="[THT]"]
  HC-SR04_Sensor_1 = HC-SR04 Ultrasonic Distance Sensor
  M2 = RioRand LM2596
  Bat1 = battery_holder_single_18650 [part_number=1]
  Bat2 = battery_holder_single_18650
  Bat3 = battery_holder_single_18650
  U1 = RELAY [package=relay-jzc]
  Componente3 = Motor Driver 1A Dual TB6612FNG
  ESP32 = DOIT Esp32 DevKit v1 (30 pins long, 11 pins width) [part_number=ESP32S-PIN30]
  DC_Mot_Enc1 = DC Motor with two-phase hall-encoder [part_number=VT-E-G25A-06-177E]
  J2 = Basic Servo
  BAT1 = 3-USB-Power-Bank-Battery-Pack
  U3 = SWITCH_SPDT [package=kps-1290]
  HC-SR04_Sensor_2 = HC-SR04 Ultrasonic Distance Sensor
  HC-SR04_Sensor_3 = HC-SR04 Ultrasonic Distance Sensor

nets:
  N1: Raspberry_Pi_1.GPIO3, Raspberry_Pi_1.GPIO4, J2.pulse
  GND: Raspberry_Pi_1.GND, S1.Pin_3, S1.Pin_4, S2.Pin_3, S2.Pin_4, M2.Pin_2, Bat1.+#0, U1.NC, U1.NO, Componente3.GND, ESP32.GND, DC_Mot_Enc1.pin2
  N2: S1.Pin_1, S1.Pin_2, ESP32.D12
  N3: S2.Pin_1, S2.Pin_2, ESP32.D13
  VCC: HC-SR04_Sensor_1.VCC, M2.Pin_3, J2.vcc, HC-SR04_Sensor_2.VCC, HC-SR04_Sensor_3.VCC
  N4: HC-SR04_Sensor_1.TRIG, ESP32.D32
  N5: HC-SR04_Sensor_1.ECHO, ESP32.D33
  GND_2: HC-SR04_Sensor_1.GND, M2.Pin_4, J2.gnd, HC-SR04_Sensor_2.GND, HC-SR04_Sensor_3.GND
  N6: M2.Pin_1, U1.COIL1, Componente3.VM
  N7: Bat1.+#1, Bat2.+#0
  N8: Bat2.+#1, Bat3.+#0
  N9: Bat3.+#1, U1.MAIN
  VCC_2: U1.COIL2, Componente3.VCC, ESP32.3V3, DC_Mot_Enc1.pin5
  N10: Componente3.A02, DC_Mot_Enc1.pin6
  N11: Componente3.A01, DC_Mot_Enc1.pin1
  N12: Componente3.PWMA, ESP32.D25
  N13: Componente3.AIN2, ESP32.D26
  N14: Componente3.AIN1, ESP32.D27
  N15: Componente3.STBY, ESP32.D14
  N16: ESP32.D4, DC_Mot_Enc1.pin3
  N17: ESP32.RX2, HC-SR04_Sensor_3.TRIG
  N18: ESP32.TX2, HC-SR04_Sensor_3.ECHO
  N19: ESP32.D5, DC_Mot_Enc1.pin4
  N20: ESP32.D18, HC-SR04_Sensor_2.TRIG
  N21: ESP32.D19, HC-SR04_Sensor_2.ECHO
  N22: BAT1.5V+, U3.O
  N23: BAT1.GND, U3.S

custom parts:
  battery_holder_single_18650: single 18650 battery holder
  DOIT Esp32 DevKit v1 (30 pins long, 11 pins width): The DOIT Esp32 DevKit v1 is one of the development board created by DOIT to evaluate the ESP-WROOM-32 module. It is based on the ESP32 microcontroller that boasts Wifi, Bluetooth, Ethernet and Low Power support all in a single chip. (vanepp) made breadboard work, adjusted pin numbering and labels and reduced size of schematic and cleaned up pcb. This chip is 30pins long (2 x15) and 11 pins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
  3-USB-Power-Bank-Battery-Pack: INIU B61 Power Bank 10000mAh, 3-Port Design.
